// Digital circuit BoothsMultiplierPart1.dig as structural Verilog
module BoothsMultiplierPart1 (
  input  CLK,
  input  CLR,
  input  [12:0] MULTIPLICAND,
  input  [12:0] MULTIPLIER,
  output DONE,
  output [1:0] OP_DONE,
  output [25:0] RESULT
);

  wire controlunit_1_p4, INIT_INPUT, LOAD_INPUT, not_1_out, not_2_out, or_1_out, or_2_out, SHIFT_INPUT;
  wire [12:0] MULTIPLICAND_p8;
  wire [13:0] ACCUMULATOR_p6, add_1_s, bitextender_1_out, bitextender_2_out, bitextender_3_out,
       MULTIPLICAND_DATA, sub_1_s;

  // ControlUnit controlunit_1: pin names not known; wires that end beside it: CLK, CLR, DONE, controlunit_1_p4, LOAD_INPUT, SHIFT_INPUT
  not not_1 (not_1_out, controlunit_1_p4);
  Monoflop monoflop_1 (.C(not_1_out), .R(LOAD_INPUT), .Q(INIT_INPUT));  // open: nQ
  or or_1 (or_1_out, LOAD_INPUT, INIT_INPUT, SHIFT_INPUT);
  // Shifter ACCUMULATOR: pin names not known; wires that end beside it: or_1_out, INIT_INPUT, LOAD_INPUT, SHIFT_INPUT, RESULT[25], ACCUMULATOR_p6[12:0], RESULT[25:13]
  // Probe on RESULT[25:13]
  // Probe on ACCUMULATOR_p6
  // Probe on ACCUMULATOR_p6
  // Probe on {RESULT[25:1], OP_DONE[1]}
  BitExtender #(.inputBits(13), .outputBits(14)) bitextender_1 (.in(RESULT[25:13]), .out(bitextender_1_out));
  Add #(.Bits(14)) add_1 (.a(bitextender_1_out), .b(MULTIPLICAND_DATA), .c_i(1'b0), .s(add_1_s));  // open: c_o
  // Probe on bitextender_2_out
  // Probe on bitextender_1_out
  BitExtender #(.inputBits(13), .outputBits(14)) bitextender_2 (.in(RESULT[25:13]), .out(bitextender_2_out));
  BitExtender #(.inputBits(13), .outputBits(14)) bitextender_3 (.in(RESULT[25:13]), .out(bitextender_3_out));
  Multiplexer #(.Selector_Bits(2), .Bits(14)) multiplexer_1 (
    .sel(OP_DONE), .in_0(bitextender_3_out), .in_1(add_1_s), .in_2(sub_1_s), .in_3(bitextender_2_out),
    .out(ACCUMULATOR_p6));
  // Probe on {RESULT[25:1], OP_DONE[1]}
  or or_2 (or_2_out, INIT_INPUT, SHIFT_INPUT);
  // Shifter MULTIPLIER: pin names not known; wires that end beside it: MULTIPLIER, or_2_out, 1'b0, INIT_INPUT, SHIFT_INPUT, RESULT[13], 13'hfff, {RESULT[12:1], OP_DONE[1]}
  // Probe on 13'hfff
  Sub #(.Bits(14)) sub_1 (.a(bitextender_1_out), .b(MULTIPLICAND_DATA), .c_i(1'b0), .s(sub_1_s));  // open: c_o
  // Probe on {RESULT[12:1], OP_DONE[1]}
  // Probe on OP_DONE[1]
  // Probe on OP_DONE[1]
  not not_2 (not_2_out, LOAD_INPUT);
  // Probe on OP_DONE
  // Shifter MULTIPLICAND: pin names not known; wires that end beside it: MULTIPLICAND, INIT_INPUT, 1'b0, INIT_INPUT, 1'b0, 1'b0, 13'h1000, MULTIPLICAND_p8
  D_FF F1 (.D(OP_DONE[1]), .C(not_2_out), .Q(OP_DONE[0]));  // open: nQ
  // Probe on 13'h1000
  // Probe on OP_DONE[0]
  // Probe on MULTIPLICAND_p8
  // Probe on MULTIPLICAND_p8
  BitExtender #(.inputBits(13), .outputBits(14)) bitextender_4 (.in(MULTIPLICAND_p8), .out(MULTIPLICAND_DATA));

  assign RESULT[0] = OP_DONE[1];

  // Other names for the same wires on the sheet: ACCUMULATOR_DATA[12:0] = RESULT[25:13]
endmodule
