// Digital circuit BoothsMultiplierPart2.dig as structural Verilog
module BoothsMultiplierPart2 (
  input  CLK,
  input  CLR,
  input  [12:0] MULTIPLICAND,
  input  [12:0] MULTIPLIER,
  output DONE,
  output [1:0] OP_DONE,
  output [25:0] RESULT
);

  wire controlunit_1_p4, INIT_INPUT, LOAD_INPUT, not_1_out, not_2_out, or_1_out, or_2_out, SHIFT_INPUT;
  wire [12:0] ACCUMULATOR_p6, add_1_s, MULTIPLICAND_DATA, sub_1_s;

  // ControlUnit controlunit_1: pin names not known; wires that end beside it: CLK, CLR, DONE, controlunit_1_p4, LOAD_INPUT, SHIFT_INPUT
  not not_1 (not_1_out, controlunit_1_p4);
  Monoflop monoflop_1 (.C(not_1_out), .R(LOAD_INPUT), .Q(INIT_INPUT));  // open: nQ
  or or_1 (or_1_out, LOAD_INPUT, INIT_INPUT, SHIFT_INPUT);
  // Probe on RESULT[25]
  // Shifter ACCUMULATOR: pin names not known; wires that end beside it: or_1_out, INIT_INPUT, LOAD_INPUT, SHIFT_INPUT, RESULT[25], ACCUMULATOR_p6, RESULT[25:13]
  // Probe on RESULT[25:13]
  // Probe on ACCUMULATOR_p6
  // Probe on ACCUMULATOR_p6
  // Probe on {RESULT[25:1], OP_DONE[1]}
  Add #(.Bits(13)) add_1 (.a(RESULT[25:13]), .b(MULTIPLICAND_DATA), .c_i(1'b0), .s(add_1_s));  // open: c_o
  // Probe on RESULT[25:13]
  // Probe on RESULT[25:13]
  Multiplexer #(.Selector_Bits(2), .Bits(13)) multiplexer_1 (
    .sel(OP_DONE), .in_0(RESULT[25:13]), .in_1(add_1_s), .in_2(sub_1_s), .in_3(RESULT[25:13]),
    .out(ACCUMULATOR_p6));
  // Probe on {RESULT[25:1], OP_DONE[1]}
  or or_2 (or_2_out, INIT_INPUT, SHIFT_INPUT);
  // Shifter MULTIPLIER: pin names not known; wires that end beside it: MULTIPLIER, or_2_out, 1'b0, INIT_INPUT, SHIFT_INPUT, RESULT[13], 13'h1000, {RESULT[12:1], OP_DONE[1]}
  // Probe on 13'h1000
  Sub #(.Bits(13)) sub_1 (.a(RESULT[25:13]), .b(MULTIPLICAND_DATA), .c_i(1'b0), .s(sub_1_s));  // open: c_o
  // Probe on {RESULT[12:1], OP_DONE[1]}
  // Probe on OP_DONE[1]
  // Probe on OP_DONE[1]
  not not_2 (not_2_out, LOAD_INPUT);
  // Probe on OP_DONE
  // Shifter MULTIPLICAND: pin names not known; wires that end beside it: MULTIPLICAND, INIT_INPUT, 1'b0, INIT_INPUT, 1'b0, 1'b0, 13'hfff, MULTIPLICAND_DATA
  D_FF F1 (.D(OP_DONE[1]), .C(not_2_out), .Q(OP_DONE[0]));  // open: nQ
  // Probe on 13'hfff
  // Probe on OP_DONE[0]
  // Probe on MULTIPLICAND_DATA
  // Probe on MULTIPLICAND_DATA

  assign RESULT[0] = OP_DONE[1];

  // Other names for the same wires on the sheet: OP_INPUT[1:0] = OP_DONE; ACCUMULATOR_DATA[12:0] = RESULT[25:13]
endmodule
