// Digital circuit BoothsMultiplierPart4.dig as structural Verilog
module BoothsMultiplierPart4 (
  input  CLK,
  input  CLR,
  input  [12:0] MULTIPLICAND,
  input  [12:0] MULTIPLIER,
  output DONE,
  output [1:0] OP_DONE,
  output [25:0] RESULT
);

  wire and_1_out, and_2_out, and_3_out, d_ff_1_q, INIT_FIRST, INIT_INPUT, LOAD_INPUT, multiplexer_1_out,
       not_1_out, not_2_out, not_3_out, or_1_out, or_2_out, or_3_out, or_4_out, SHIFT_INPUT, xor_1_out;
  wire [12:0] ACCUMULATOR_p6, add_1_s, MULTIPLICAND_DATA, sub_1_s;

  not not_1 (not_1_out, MULTIPLICAND_DATA[12]);
  Multiplexer multiplexer_1 (.sel(OP_DONE[0]), .in_0(not_1_out), .in_1(MULTIPLICAND_DATA[12]), .out(multiplexer_1_out));
  // ControlUnit controlunit_1: pin names not known; wires that end beside it: CLK, CLR, DONE, INIT_FIRST, LOAD_INPUT, SHIFT_INPUT
  and and_1 (and_1_out, ~INIT_FIRST, multiplexer_1_out);  // And
  and and_2 (and_2_out, xor_1_out, ~INIT_INPUT);  // And
  xor xor_1 (xor_1_out, OP_DONE[0], OP_DONE[1]);
  or or_1 (or_1_out, and_2_out, INIT_FIRST);
  not not_2 (not_2_out, INIT_FIRST);
  D_FF d_ff_1 (.D(and_1_out), .C(or_1_out), .Q(d_ff_1_q));  // open: nQ
  Monoflop monoflop_1 (.C(not_2_out), .R(LOAD_INPUT), .Q(INIT_INPUT));  // open: nQ
  or or_2 (or_2_out, LOAD_INPUT, INIT_INPUT, SHIFT_INPUT);
  // Probe on d_ff_1_q
  // Shifter ACCUMULATOR: pin names not known; wires that end beside it: or_2_out, INIT_INPUT, LOAD_INPUT, SHIFT_INPUT, d_ff_1_q, ACCUMULATOR_p6, RESULT[25:13]
  // Probe on RESULT[25:13]
  // Probe on ACCUMULATOR_p6
  // Probe on ACCUMULATOR_p6
  // Probe on {RESULT[25:1], OP_DONE[1]}
  Add #(.Bits(13)) add_1 (.a(RESULT[25:13]), .b(MULTIPLICAND_DATA), .c_i(1'b0), .s(add_1_s));  // open: c_o
  // Probe on RESULT[25:13]
  // Probe on RESULT[25:13]
  Multiplexer #(.Selector_Bits(2), .Bits(13)) multiplexer_2 (
    .sel(OP_DONE), .in_0(RESULT[25:13]), .in_1(add_1_s), .in_2(sub_1_s), .in_3(RESULT[25:13]),
    .out(ACCUMULATOR_p6));
  // Probe on {RESULT[25:1], OP_DONE[1]}
  or or_3 (or_3_out, INIT_INPUT, SHIFT_INPUT);
  // Shifter MULTIPLIER: pin names not known; wires that end beside it: MULTIPLIER, or_3_out, 1'b0, INIT_INPUT, SHIFT_INPUT, RESULT[13], 13'hfff, {RESULT[12:1], OP_DONE[1]}
  // Probe on 13'hfff
  Sub #(.Bits(13)) sub_1 (.a(RESULT[25:13]), .b(MULTIPLICAND_DATA), .c_i(1'b0), .s(sub_1_s));  // open: c_o
  // Probe on {RESULT[12:1], OP_DONE[1]}
  // Probe on OP_DONE[1]
  and and_3 (and_3_out, ~INIT_FIRST, OP_DONE[1]);  // And
  // Probe on OP_DONE[1]
  or or_4 (or_4_out, not_3_out, INIT_FIRST);
  not not_3 (not_3_out, LOAD_INPUT);
  // Probe on OP_DONE
  // Shifter MULTIPLICAND: pin names not known; wires that end beside it: MULTIPLICAND, INIT_INPUT, 1'b0, INIT_INPUT, 1'b0, 1'b0, 13'h1000, MULTIPLICAND_DATA
  D_FF F1 (.D(and_3_out), .C(or_4_out), .Q(OP_DONE[0]));  // open: nQ
  // Probe on 13'h1000
  // Probe on OP_DONE[0]
  // Probe on MULTIPLICAND_DATA
  // Probe on MULTIPLICAND_DATA

  assign RESULT[0] = OP_DONE[1];

  // Other names for the same wires on the sheet: OP_DATA[1:0] = OP_DONE; ACCUMULATOR_DATA[12:0] = RESULT[25:13]
endmodule
