// Digital circuit BoothsMultiplierPart4.dig as structural Verilog
module BoothsMultiplierPart4 (
  input  CLK,
  input  CLR,
  input  [12:0] MULTIPLICAND,
  input  [12:0] MULTIPLIER,
  output DONE,
  output [1:0] OP_DONE,
  output [25:0] RESULT
);

  wire and_1_out, and_2_out, and_3_out, comparator_1_eq, comparator_2_eq, d_ff_as_1_q, INIT_FIRST,
       INIT_INPUT, LOAD_INPUT, multiplexer_1_out, not_1_out, not_2_out, not_3_out, or_1_out, or_2_out,
       or_3_out, RESULT_0, SHIFT_INPUT, xor_1_out;
  wire [12:0] ACCUMULATOR_DATA, ACCUMULATOR_p6, add_1_s, MULTIPLICAND_DATA, sub_1_s;
  wire [12:1] MULTIPLIER_p7;

  not not_1 (not_1_out, MULTIPLICAND_DATA[12]);
  Multiplexer #(.Selector_Bits(2)) multiplexer_1 (
    .sel(OP_DONE), .in_0(and_1_out), .in_1(MULTIPLICAND_DATA[12]), .in_2(not_1_out), .in_3(and_1_out),
    .out(multiplexer_1_out));
  // ControlUnit controlunit_1: pin names not known; wires that end beside it: CLK, CLR, DONE, INIT_FIRST, LOAD_INPUT, SHIFT_INPUT
  Comparator #(.Bits(13)) comparator_1 (.a(MULTIPLICAND), .b({13{1'b0}}), .eq(comparator_1_eq));  // open: gt, lt
  Comparator #(.Bits(13)) comparator_2 (.a(MULTIPLIER), .b({13{1'b0}}), .eq(comparator_2_eq));  // open: gt, lt
  and and_1 (and_1_out, ~INIT_FIRST, multiplexer_1_out);  // And
  and and_2 (and_2_out, xor_1_out, not_2_out);
  xor xor_1 (xor_1_out, OP_DONE[0], OP_DONE[1]);
  not not_2 (not_2_out, LOAD_INPUT);
  or or_1 (or_1_out, comparator_1_eq, comparator_2_eq);
  D_FF_AS d_ff_as_1 (.Set(1'b0), .D(and_1_out), .C(and_2_out), .Clr(INIT_FIRST), .Q(d_ff_as_1_q));  // open: nQ
  D_FF_AS d_ff_as_2 (.Set(1'b0), .D(INIT_FIRST), .C(CLK), .Clr(LOAD_INPUT), .Q(INIT_INPUT));  // open: nQ
  and and_3 (and_3_out, or_1_out, INIT_FIRST);
  or or_2 (or_2_out, LOAD_INPUT, INIT_INPUT, SHIFT_INPUT);
  // Probe on d_ff_as_1_q
  // Shifter ACCUMULATOR: pin names not known; wires that end beside it: or_2_out, INIT_INPUT, LOAD_INPUT, SHIFT_INPUT, d_ff_as_1_q, ACCUMULATOR_p6, ACCUMULATOR_DATA
  D_FF_AS d_ff_as_3 (.Set(1'b0), .D(and_3_out), .C(INIT_INPUT), .Clr(1'b0), .Q(RESULT_0));  // open: nQ
  // Probe on ACCUMULATOR_DATA
  // Probe on ACCUMULATOR_p6
  // Probe on ACCUMULATOR_p6
  Multiplexer #(.Bits(26)) multiplexer_2 (
    .sel(RESULT_0), .in_0({ACCUMULATOR_DATA, MULTIPLIER_p7, OP_DONE[1]}), .in_1({26{1'b0}}), .out(RESULT));
  // Probe on RESULT
  Add #(.Bits(13)) add_1 (.a(ACCUMULATOR_DATA), .b(MULTIPLICAND_DATA), .c_i(1'b0), .s(add_1_s));  // open: c_o
  // Probe on ACCUMULATOR_DATA
  // Probe on ACCUMULATOR_DATA
  Multiplexer #(.Selector_Bits(2), .Bits(13)) multiplexer_3 (
    .sel(OP_DONE), .in_0(ACCUMULATOR_DATA), .in_1(add_1_s), .in_2(sub_1_s), .in_3(ACCUMULATOR_DATA),
    .out(ACCUMULATOR_p6));
  // Probe on RESULT
  or or_3 (or_3_out, INIT_INPUT, SHIFT_INPUT);
  // Shifter MULTIPLIER: pin names not known; wires that end beside it: or_3_out, 1'b0, INIT_INPUT, SHIFT_INPUT, ACCUMULATOR_DATA[0], MULTIPLIER, {MULTIPLIER_p7, OP_DONE[1]}
  // Probe on MULTIPLIER
  Sub #(.Bits(13)) sub_1 (.a(ACCUMULATOR_DATA), .b(MULTIPLICAND_DATA), .c_i(1'b0), .s(sub_1_s));  // open: c_o
  // Probe on {MULTIPLIER_p7, OP_DONE[1]}
  // Probe on OP_DONE[1]
  // Probe on OP_DONE[1]
  not not_3 (not_3_out, LOAD_INPUT);
  // Probe on OP_DONE
  // Shifter MULTIPLICAND: pin names not known; wires that end beside it: INIT_INPUT, 1'b0, INIT_INPUT, 1'b0, 1'b0, MULTIPLICAND, MULTIPLICAND_DATA
  D_FF_AS d_ff_as_4 (.Set(1'b0), .D(OP_DONE[1]), .C(not_3_out), .Clr(INIT_FIRST), .Q(OP_DONE[0]));  // open: nQ
  // Probe on MULTIPLICAND
  // Probe on OP_DONE[0]
  // Probe on MULTIPLICAND_DATA
  // Probe on MULTIPLICAND_DATA

  // Other names for the same wires on the sheet: OP_DATA[1:0] = OP_DONE; CLK_INPUT = CLK;
  //   MULTIPLICAND_INPUT[12:0] = MULTIPLICAND; MULTIPLIER_DATA[12:0] = MULTIPLIER
endmodule

/* Test case:
		CLK	MULTIPLIER	MULTIPLICAND	RESULT
repeat(28)	C	4		4		16
*/
