// Digital circuit LogicalEquivalanceChecking.dig as structural Verilog
module LogicalEquivalanceChecking (
  input  B,
  input  C,
  input  D,
  input  A,
  output Y_0,
  output Y_1,
  output Z_0,
  output Z_1,
  output F_0,
  output F_1
);

  wire and_1_out, and_2_out, and_3_out, and_4_out, and_5_out, and_6_out, and_7_out, and_8_out, and_9_out,
       and_10_out, and_13_out, and_14_out, or_1_out, or_2_out, or_3_out, or_4_out, or_5_out, or_6_out,
       or_7_out, xor_1_out;

  or or_1 (or_1_out, A, B);
  or or_2 (or_2_out, ~C, D);  // Or
  or or_3 (or_3_out, A, ~C);  // Or
  and and_1 (and_1_out, A, ~C);  // And
  and and_2 (and_2_out, A, D);
  and and_3 (and_3_out, C, D);
  and and_4 (and_4_out, ~A, B, ~D);  // And
  or or_4 (or_4_out, A, C);
  or or_5 (or_5_out, ~A, ~C);  // Or
  and and_5 (and_5_out, A, ~B, ~C);  // And
  and and_6 (and_6_out, ~A, ~B, C);  // And
  xor xor_1 (xor_1_out, A, B);
  and and_7 (and_7_out, ~A, B);  // And
  and and_8 (and_8_out, A, ~B);  // And
  and and_9 (and_9_out, A, B);
  and and_10 (and_10_out, ~A, ~B);  // And
  xnor xnor_1 (F_0, xor_1_out, C);
  or or_6 (or_6_out, and_7_out, and_8_out);
  or or_7 (or_7_out, and_9_out, and_10_out);
  or or_8 (Z_1, and_5_out, and_6_out);
  and and_11 (Y_0, or_1_out, or_2_out, or_3_out);
  or or_9 (Y_1, and_1_out, and_2_out, and_3_out, and_4_out);
  and and_12 (Z_0, or_4_out, ~B, or_5_out);  // And
  and and_13 (and_13_out, or_6_out, C);
  and and_14 (and_14_out, ~C, or_7_out);  // And
  // XOr xor_2 has open pins: In_1=Y_0, In_2=Y_1, out=open
  // XOr xor_3 has open pins: In_1=Z_0, In_2=Z_1, out=open
  or or_10 (F_1, and_13_out, and_14_out);
  // XOr xor_4 has open pins: In_1=F_0, In_2=F_1, out=open
endmodule
