// Digital circuit SingleLevelCLA.dig as structural Verilog
module SingleLevelCLA (
);

  wire c0, c1, c2, c3, c4, g0, g1, g2, g3, p0, p1, p2, p3, s0, s1, s2, s3;

  generator generator_1 (.c_i(c3), .g_i(g3), .p_i(p3));  // open: x_i, y_i
  generator generator_2 (.c_i(c2), .g_i(g2), .p_i(p2));  // open: x_i, y_i
  generator generator_3 (.c_i(c1), .g_i(g1), .p_i(p1));  // open: x_i, y_i
  _4BitCLA _4bitcla_1 (
    .c_0(c0), .g_0(g0), .p_0(p0), .g_1(g1), .p_1(p1), .g_2(g2), .p_2(p2), .g_3(g3), .p_3(p3), .c_1(c1),
    .c_2(c2), .c_3(c3), .s_0(s0), .s_1(s1), .s_2(s2), .s_3(s3), .c_4(c4));
  generator generator_4 (.c_i(c0), .g_i(g0), .p_i(p0));  // open: x_i, y_i
endmodule
