// Digital circuit 2421SingleLevelCLA_D.dig as structural Verilog
module _2421SingleLevelCLA_D (
  input  Cin,
  input  [15:0] X,
  input  [15:0] Y,
  output Cout,
  output [15:0] S
);

  wire _4bitcla_extended_d_2_c_out, _4bitcla_extended_d_3_c_out, _4bitcla_extended_d_4_c_out;
  wire [3:0] _4bitcla_extended_d_1_s, _4bitcla_extended_d_2_s, _4bitcla_extended_d_3_s,
       _4bitcla_extended_d_4_s, _4bitpg_generatord_1_g, _4bitpg_generatord_1_p, _4bitpg_generatord_2_g,
       _4bitpg_generatord_2_p, _4bitpg_generatord_3_g, _4bitpg_generatord_3_p, _4bitpg_generatord_4_g,
       _4bitpg_generatord_4_p;

  _4BitPG_GeneratorD _4bitpg_generatord_1 (
    .x(X[15:12]), .y(Y[15:12]), .p(_4bitpg_generatord_1_p), .g(_4bitpg_generatord_1_g));
  _4BitCLA_Extended_D _4bitcla_extended_d_1 (
    .c_0(_4bitcla_extended_d_2_c_out), .p(_4bitpg_generatord_1_p), .g(_4bitpg_generatord_1_g),
    .S(_4bitcla_extended_d_1_s), .c_out(Cout));  // open: P_2, G_2, c1, c2, c3
  // CorrectorD correctord_1: pin names not known; wires that end beside it: Cout, S[15:12], _4bitcla_extended_d_1_s
  _4BitPG_GeneratorD _4bitpg_generatord_2 (
    .x(X[11:8]), .y(Y[11:8]), .p(_4bitpg_generatord_2_p), .g(_4bitpg_generatord_2_g));
  _4BitCLA_Extended_D _4bitcla_extended_d_2 (
    .c_0(_4bitcla_extended_d_3_c_out), .p(_4bitpg_generatord_2_p), .g(_4bitpg_generatord_2_g),
    .S(_4bitcla_extended_d_2_s), .c_out(_4bitcla_extended_d_2_c_out));  // open: P_2, G_2, c1, c2, c3
  // CorrectorD correctord_2: pin names not known; wires that end beside it: _4bitcla_extended_d_2_c_out, S[11:8], _4bitcla_extended_d_2_s
  _4BitPG_GeneratorD _4bitpg_generatord_3 (
    .x(X[7:4]), .y(Y[7:4]), .p(_4bitpg_generatord_3_p), .g(_4bitpg_generatord_3_g));
  _4BitCLA_Extended_D _4bitcla_extended_d_3 (
    .c_0(_4bitcla_extended_d_4_c_out), .p(_4bitpg_generatord_3_p), .g(_4bitpg_generatord_3_g),
    .S(_4bitcla_extended_d_3_s), .c_out(_4bitcla_extended_d_3_c_out));  // open: P_2, G_2, c1, c2, c3
  // CorrectorD correctord_3: pin names not known; wires that end beside it: _4bitcla_extended_d_3_c_out, S[7:4], _4bitcla_extended_d_3_s
  _4BitPG_GeneratorD _4bitpg_generatord_4 (
    .x(X[3:0]), .y(Y[3:0]), .p(_4bitpg_generatord_4_p), .g(_4bitpg_generatord_4_g));
  _4BitCLA_Extended_D _4bitcla_extended_d_4 (
    .c_0(Cin), .p(_4bitpg_generatord_4_p), .g(_4bitpg_generatord_4_g), .S(_4bitcla_extended_d_4_s),
    .c_out(_4bitcla_extended_d_4_c_out));  // open: P_2, G_2, c1, c2, c3
  // CorrectorD correctord_4: pin names not known; wires that end beside it: _4bitcla_extended_d_4_c_out, S[3:0], _4bitcla_extended_d_4_s
endmodule

/* Test case:
X		Y		S
0x001E		0x44EF		0x4B0D
0x001E		0x44F0		0x4B0E
0x001E		0x44F1		0x4B0F
0x001E		0x44F2		0x4B10
0x001E		0x44F3		0x4B11
0x001E		0x44F4		0x4B12
0x001E		0x44FB		0x4B13
0x001E		0x44FC		0x4B14
0x001E		0x44FD		0x4B1B
0x001E		0x44FE		0x4B1C
0x001E		0x44FF		0x4B1D
0x001E		0x4B00		0x4B1E
0x001E		0x4B01		0x4B1F
0x001E		0x4B02		0x4B20
0x001E		0x4B03		0x4B21
0x001E		0x4B04		0x4B22
0x001E		0x4B0B		0x4B23
0x001E		0x4B0C		0x4B24
0x001E		0x4B0D		0x4B2B
0x001E		0x4B0E		0x4B2C
0x001E		0x4B0F		0x4B2D
0x001E		0x4B10		0x4B2E
0x001E		0x4B11		0x4B2F
0x001E		0x4B12		0x4B30
0x001E		0x4B13		0x4B31
0x001E		0x4B14		0x4B32
0x001E		0x4B1B		0x4B33
0x001E		0x4B1C		0x4B34
0x001E		0x4B1D		0x4B3B
0x001E		0x4B1E		0x4B3C
0x001E		0x4B1F		0x4B3D
0x001E		0x4B20		0x4B3E
0x001E		0x4B21		0x4B3F
0x001E		0x4B22		0x4B40
0x001E		0x4B23		0x4B41
0x001E		0x4B24		0x4B42
0x001E		0x4B2B		0x4B43
0x001E		0x4B2C		0x4B44
0x001E		0x4B2D		0x4B4B
0x001E		0x4B2E		0x4B4C
0x001E		0x4B2F		0x4B4D
0x001E		0x4B30		0x4B4E
0x001E		0x4B31		0x4B4F
0x001E		0x4B32		0x4BB0
0x001E		0x4B33		0x4BB1
0x001E		0x4B34		0x4BB2
0x001E		0x4B3B		0x4BB3
0x001E		0x4B3C		0x4BB4
0x001E		0x4B3D		0x4BBB
0x001E		0x4B3E		0x4BBC
0x001E		0x4B3F		0x4BBD
0x001E		0x4B40		0x4BBE
0x001E		0x4B41		0x4BBF
0x001E		0x4B42		0x4BC0
0x001E		0x4B43		0x4BC1
0x001E		0x4B44		0x4BC2
0x001E		0x4B4B		0x4BC3
0x001E		0x4B4C		0x4BC4
0x001E		0x4B4D		0x4BCB
0x001E		0x4B4E		0x4BCC
0x001E		0x4B4F		0x4BCD
0x001E		0x4BB0		0x4BCE
0x001E		0x4BB1		0x4BCF
0x001E		0x4BB2		0x4BD0
0x001E		0x4BB3		0x4BD1
0x001E		0x4BB4		0x4BD2
0x001E		0x4BBB		0x4BD3
0x001E		0x4BBC		0x4BD4
0x001E		0x4BBD		0x4BDB
0x001E		0x4BBE		0x4BDC
0x001E		0x4BBF		0x4BDD
0x001E		0x4BC0		0x4BDE
0x001E		0x4BC1		0x4BDF
0x001E		0x4BC2		0x4BE0
0x001E		0x4BC3		0x4BE1
0x001E		0x4BC4		0x4BE2
0x001E		0x4BCB		0x4BE3
0x001E		0x4BCC		0x4BE4
0x001E		0x4BCD		0x4BEB
0x001E		0x4BCE		0x4BEC
0x001E		0x4BCF		0x4BED
0x001E		0x4BD0		0x4BEE
0x001E		0x4BD1		0x4BEF
0x001E		0x4BD2		0x4BF0
0x001E		0x4BD3		0x4BF1
0x001E		0x4BD4		0x4BF2
0x001E		0x4BDB		0x4BF3
0x001E		0x4BDC		0x4BF4
0x001E		0x4BDD		0x4BFB
0x001E		0x4BDE		0x4BFC
0x001E		0x4BDF		0x4BFD
0x001E		0x4BE0		0x4BFE
0x001E		0x4BE1		0x4BFF
0x001E		0x4BE2		0x4C00
0x001E		0x4BE3		0x4C01
0x001E		0x4BE4		0x4C02
0x001E		0x4BEB		0x4C03
0x001E		0x4BEC		0x4C04
0x001E		0x4BED		0x4C0B
0x001E		0x4BEE		0x4C0C
0x001E		0x4BEF		0x4C0D
0x001E		0x4BF0		0x4C0E
0x001E		0x4BF1		0x4C0F
0x001E		0x4BF2		0x4C10
0x001E		0x4BF3		0x4C11
0x001E		0x4BF4		0x4C12
0x001E		0x4BFB		0x4C13
0x001E		0x4BFC		0x4C14
0x001E		0x4BFD		0x4C1B
0x001E		0x4BFE		0x4C1C
0x001E		0x4BFF		0x4C1D
0x001E		0x4C00		0x4C1E
0x001E		0x4C01		0x4C1F
0x001E		0x4C02		0x4C20
0x001E		0x4C03		0x4C21
0x001E		0x4C04		0x4C22
0x001E		0x4C0B		0x4C23
0x001E		0x4C0C		0x4C24
0x001E		0x4C0D		0x4C2B
0x001E		0x4C0E		0x4C2C
0x001E		0x4C0F		0x4C2D
0x001E		0x4C10		0x4C2E
0x001E		0x4C11		0x4C2F
0x001E		0x4C12		0x4C30
0x001E		0x4C13		0x4C31
0x001E		0x4C14		0x4C32
0x001E		0x4C1B		0x4C33
0x001E		0x4C1C		0x4C34
0x001E		0x4C1D		0x4C3B
0x001E		0x4C1E		0x4C3C
0x001E		0x4C1F		0x4C3D
0x001E		0x4C20		0x4C3E
0x001E		0x4C21		0x4C3F
0x001E		0x4C22		0x4C40
0x001E		0x4C23		0x4C41
0x001E		0x4C24		0x4C42
0x001E		0x4C2B		0x4C43
0x001E		0x4C2C		0x4C44
0x001E		0x4C2D		0x4C4B
0x001E		0x4C2E		0x4C4C
0x001E		0x4C2F		0x4C4D
0x001E		0x4C30		0x4C4E
0x001E		0x4C31		0x4C4F
0x001E		0x4C32		0x4CB0
0x001E		0x4C33		0x4CB1
0x001E		0x4C34		0x4CB2
0x001E		0x4C3B		0x4CB3
0x001E		0x4C3C		0x4CB4
0x001E		0x4C3D		0x4CBB
0x001E		0x4C3E		0x4CBC
0x001E		0x4C3F		0x4CBD
0x001E		0x4C40		0x4CBE
0x001E		0x4C41		0x4CBF
0x001E		0x4C42		0x4CC0
0x001E		0x4C43		0x4CC1
0x001E		0x4C44		0x4CC2
0x001E		0x4C4B		0x4CC3
0x001E		0x4C4C		0x4CC4
0x001E		0x4C4D		0x4CCB
0x001E		0x4C4E		0x4CCC
0x001E		0x4C4F		0x4CCD
0x001E		0x4CB0		0x4CCE
0x001E		0x4CB1		0x4CCF
0x001E		0x4CB2		0x4CD0
0x001E		0x4CB3		0x4CD1
0x001E		0x4CB4		0x4CD2
0x001E		0x4CBB		0x4CD3
0x001E		0x4CBC		0x4CD4
0x001E		0x4CBD		0x4CDB
0x001E		0x4CBE		0x4CDC
0x001E		0x4CBF		0x4CDD
0x001E		0x4CC0		0x4CDE
0x001E		0x4CC1		0x4CDF
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*/
