// Digital circuit 2421TwoLevelCLA_D.dig as structural Verilog
module _2421TwoLevelCLA_D (
  input  Cin,
  input  [15:0] X,
  input  [15:0] Y,
  output Cout,
  output [15:0] S
);

  wire correctord_2_p1, correctord_3_p1, correctord_4_p1;
  wire [3:0] _4bitcla_extended_d_1_s, _4bitcla_extended_d_2_s, _4bitcla_extended_d_3_s,
       _4bitcla_extended_d_4_s, _4bitpg_generatord_1_g, _4bitpg_generatord_1_p, _4bitpg_generatord_2_g,
       _4bitpg_generatord_2_p, _4bitpg_generatord_3_g, _4bitpg_generatord_3_p, _4bitpg_generatord_4_g,
       _4bitpg_generatord_4_p, G, P;

  _4BitPG_GeneratorD _4bitpg_generatord_1 (
    .x(X[15:12]), .y(Y[15:12]), .p(_4bitpg_generatord_1_p), .g(_4bitpg_generatord_1_g));
  _4BitCLA_Extended_D _4bitcla_extended_d_1 (
    .c_0(correctord_2_p1), .p(_4bitpg_generatord_1_p), .g(_4bitpg_generatord_1_g),
    .S(_4bitcla_extended_d_1_s), .P_2(P[3]), .G_2(G[3]));  // open: c1, c2, c3, c_out
  // CorrectorD correctord_1: pin names not known; wires that end beside it: Cout, S[15:12], _4bitcla_extended_d_1_s
  _4BitPG_GeneratorD _4bitpg_generatord_2 (
    .x(X[11:8]), .y(Y[11:8]), .p(_4bitpg_generatord_2_p), .g(_4bitpg_generatord_2_g));
  _4BitCLA_Extended_D _4bitcla_extended_d_2 (
    .c_0(correctord_3_p1), .p(_4bitpg_generatord_2_p), .g(_4bitpg_generatord_2_g),
    .S(_4bitcla_extended_d_2_s), .P_2(P[2]), .G_2(G[2]));  // open: c1, c2, c3, c_out
  // CorrectorD correctord_2: pin names not known; wires that end beside it: correctord_2_p1, S[11:8], _4bitcla_extended_d_2_s
  _4BitPG_GeneratorD _4bitpg_generatord_3 (
    .x(X[7:4]), .y(Y[7:4]), .p(_4bitpg_generatord_3_p), .g(_4bitpg_generatord_3_g));
  _4BitCLA_Extended_D _4bitcla_extended_d_3 (
    .c_0(correctord_4_p1), .p(_4bitpg_generatord_3_p), .g(_4bitpg_generatord_3_g),
    .S(_4bitcla_extended_d_3_s), .P_2(P[1]), .G_2(G[1]));  // open: c1, c2, c3, c_out
  // CorrectorD correctord_3: pin names not known; wires that end beside it: correctord_3_p1, S[7:4], _4bitcla_extended_d_3_s
  _4BitPG_GeneratorD _4bitpg_generatord_4 (
    .x(X[3:0]), .y(Y[3:0]), .p(_4bitpg_generatord_4_p), .g(_4bitpg_generatord_4_g));
  _4BitCLA_Extended_D _4bitcla_extended_d_4 (
    .c_0(Cin), .p(_4bitpg_generatord_4_p), .g(_4bitpg_generatord_4_g), .S(_4bitcla_extended_d_4_s),
    .P_2(P[0]), .G_2(G[0]));  // open: c1, c2, c3, c_out
  // CorrectorD correctord_4: pin names not known; wires that end beside it: correctord_4_p1, S[3:0], _4bitcla_extended_d_4_s
  _4BitCLA_Extended_D _4bitcla_extended_d_5 (
    .c_0(Cin), .p(P), .g(G), .c1(correctord_4_p1), .c2(correctord_3_p1), .c3(correctord_2_p1), .c_out(Cout));  // open: S, P_2, G_2
endmodule

/* Test case:
X		Y		S
0x00FD		0x00F3		0x01F0
0x00FD		0x00F4		0x01F1
0x00FD		0x00FB		0x01F2
0x00FD		0x00FC		0x01F3
0x00FD		0x00FD		0x01F4
0x00FD		0x00FE		0x01FB
0x00FD		0x00FF		0x01FC
0x00FE		0x0000		0x00FE
0x00FE		0x0001		0x00FF
0x00FE		0x0002		0x0100
0x00FE		0x0003		0x0101
0x00FE		0x0004		0x0102
0x00FE		0x000B		0x0103
0x00FE		0x000C		0x0104
0x00FE		0x000D		0x010B
0x00FE		0x000E		0x010C
0x00FE		0x000F		0x010D
0x00FE		0x0010		0x010E
0x00FE		0x0011		0x010F
0x00FE		0x0012		0x0110
0x00FE		0x0013		0x0111
0x00FE		0x0014		0x0112
0x00FE		0x001B		0x0113
0x00FE		0x001C		0x0114
0x00FE		0x001D		0x011B
0x00FE		0x001E		0x011C
0x00FE		0x001F		0x011D
0x00FE		0x0020		0x011E
0x00FE		0x0021		0x011F
0x00FE		0x0022		0x0120
0x00FE		0x0023		0x0121
0x00FE		0x0024		0x0122
0x00FE		0x002B		0x0123
0x00FE		0x002C		0x0124
0x00FE		0x002D		0x012B
0x00FE		0x002E		0x012C
0x00FE		0x002F		0x012D
0x00FE		0x0030		0x012E
0x00FE		0x0031		0x012F
0x00FE		0x0032		0x0130
0x00FE		0x0033		0x0131
0x00FE		0x0034		0x0132
0x00FE		0x003B		0x0133
0x00FE		0x003C		0x0134
0x00FE		0x003D		0x013B
0x00FE		0x003E		0x013C
0x00FE		0x003F		0x013D
0x00FE		0x0040		0x013E
0x00FE		0x0041		0x013F
0x00FE		0x0042		0x0140
0x00FE		0x0043		0x0141
0x00FE		0x0044		0x0142
0x00FE		0x004B		0x0143
0x00FE		0x004C		0x0144
0x00FE		0x004D		0x014B
0x00FE		0x004E		0x014C
0x00FE		0x004F		0x014D
0x00FE		0x00B0		0x014E
0x00FE		0x00B1		0x014F
0x00FE		0x00B2		0x01B0
0x00FE		0x00B3		0x01B1
0x00FE		0x00B4		0x01B2
0x00FE		0x00BB		0x01B3
0x00FE		0x00BC		0x01B4
0x00FE		0x00BD		0x01BB
0x00FE		0x00BE		0x01BC
0x00FE		0x00BF		0x01BD
0x00FE		0x00C0		0x01BE
0x00FE		0x00C1		0x01BF
0x00FE		0x00C2		0x01C0
0x00FE		0x00C3		0x01C1
0x00FE		0x00C4		0x01C2
0x00FE		0x00CB		0x01C3
0x00FE		0x00CC		0x01C4
0x00FE		0x00CD		0x01CB
0x00FE		0x00CE		0x01CC
0x00FE		0x00CF		0x01CD
0x00FE		0x00D0		0x01CE
0x00FE		0x00D1		0x01CF
0x00FE		0x00D2		0x01D0
0x00FE		0x00D3		0x01D1
0x00FE		0x00D4		0x01D2
0x00FE		0x00DB		0x01D3
0x00FE		0x00DC		0x01D4
0x00FE		0x00DD		0x01DB
0x00FE		0x00DE		0x01DC
0x00FE		0x00DF		0x01DD
0x00FE		0x00E0		0x01DE
0x00FE		0x00E1		0x01DF
0x00FE		0x00E2		0x01E0
0x00FE		0x00E3		0x01E1
0x00FE		0x00E4		0x01E2
0x00FE		0x00EB		0x01E3
0x00FE		0x00EC		0x01E4
0x00FE		0x00ED		0x01EB
0x00FE		0x00EE		0x01EC
0x00FE		0x00EF		0x01ED
0x00FE		0x00F0		0x01EE
0x00FE		0x00F1		0x01EF
0x00FE		0x00F2		0x01F0
0x00FE		0x00F3		0x01F1
0x00FE		0x00F4		0x01F2
0x00FE		0x00FB		0x01F3
0x00FE		0x00FC		0x01F4
0x00FE		0x00FD		0x01FB
0x00FE		0x00FE		0x01FC
0x00FE		0x00FF		0x01FD
0x00FF		0x0000		0x00FF
0x00FF		0x0001		0x0100
0x00FF		0x0002		0x0101
0x00FF		0x0003		0x0102
0x00FF		0x0004		0x0103
0x00FF		0x000B		0x0104
0x00FF		0x000C		0x010B
0x00FF		0x000D		0x010C
0x00FF		0x000E		0x010D
0x00FF		0x000F		0x010E
0x00FF		0x0010		0x010F
0x00FF		0x0011		0x0110
0x00FF		0x0012		0x0111
0x00FF		0x0013		0x0112
0x00FF		0x0014		0x0113
0x00FF		0x001B		0x0114
0x00FF		0x001C		0x011B
0x00FF		0x001D		0x011C
0x00FF		0x001E		0x011D
0x00FF		0x001F		0x011E
0x00FF		0x0020		0x011F
0x00FF		0x0021		0x0120
0x00FF		0x0022		0x0121
0x00FF		0x0023		0x0122
0x00FF		0x0024		0x0123
0x00FF		0x002B		0x0124
0x00FF		0x002C		0x012B
0x00FF		0x002D		0x012C
0x00FF		0x002E		0x012D
0x00FF		0x002F		0x012E
0x00FF		0x0030		0x012F
0x00FF		0x0031		0x0130
0x00FF		0x0032		0x0131
0x00FF		0x0033		0x0132
0x00FF		0x0034		0x0133
0x00FF		0x003B		0x0134
0x00FF		0x003C		0x013B
0x00FF		0x003D		0x013C
0x00FF		0x003E		0x013D
0x00FF		0x003F		0x013E
0x00FF		0x0040		0x013F
0x00FF		0x0041		0x0140
0x00FF		0x0042		0x0141
0x00FF		0x0043		0x0142
0x00FF		0x0044		0x0143
0x00FF		0x004B		0x0144
0x00FF		0x004C		0x014B
0x00FF		0x004D		0x014C
0x00FF		0x004E		0x014D
0x00FF		0x004F		0x014E
0x00FF		0x00B0		0x014F
0x00FF		0x00B1		0x01B0
0x00FF		0x00B2		0x01B1
0x00FF		0x00B3		0x01B2
0x00FF		0x00B4		0x01B3
0x00FF		0x00BB		0x01B4
0x00FF		0x00BC		0x01BB
0x00FF		0x00BD		0x01BC
0x00FF		0x00BE		0x01BD
0x00FF		0x00BF		0x01BE
0x00FF		0x00C0		0x01BF
0x00FF		0x00C1		0x01C0
0x00FF		0x00C2		0x01C1
0x00FF		0x00C3		0x01C2
0x00FF		0x00C4		0x01C3
0x00FF		0x00CB		0x01C4
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*/
