// Digital circuit 4BitCLA.dig as structural Verilog
module _4BitCLA (
  input  c_0,
  input  g_0,
  input  p_0,
  input  g_1,
  input  p_1,
  input  g_2,
  input  p_2,
  input  g_3,
  input  p_3,
  output c_1,
  output c_2,
  output c_3,
  output s_0,
  output s_1,
  output s_2,
  output s_3,
  output c_4
);

  wire c0, g0, g1, g2, g3, or_1_out, or_2_out, or_3_out, or_4_out, p1, p2, p3, p_0_t;

  or or_1 (or_1_out, c0, p_0_t);
  or or_2 (or_2_out, c_1, p1);
  or or_3 (or_3_out, c_2, p2);
  or or_4 (or_4_out, c_3, p3);
  and and_1 (c_1, or_1_out, g0);
  and and_2 (c_2, or_2_out, g1);
  and and_3 (c_3, or_3_out, g2);
  and and_4 (c_4, or_4_out, g3);
  xnor xnor_1 (s_0, c0, p_0_t);
  xnor xnor_2 (s_1, c_1, p1);
  xnor xnor_3 (s_2, c_2, p2);
  xnor xnor_4 (s_3, c_3, p3);

  // Other names for the same wires on the sheet: c1 = c_1; c2 = c_2; c3 = c_3; c4 = c_4; s0 = s_0; s1 = s_1; s2 = s_2;
  //   s3 = s_3
endmodule
