// Digital circuit 4BitCLA_Extended.dig as structural Verilog
module _4BitCLA_Extended (
  input  c_0,
  input  [3:0] p,
  input  [3:0] g,
  output [3:0] S,
  output P_2,
  output G_2,
  output c1,
  output c2,
  output c3,
  output c_out
);

  wire or_1_out, or_2_out, or_3_out, or_4_out, or_6_out, or_7_out, or_8_out, or_9_out, or_10_out, or_11_out;

  and and_1 (c_out, or_1_out, G_2);
  or or_1 (or_1_out, c_0, P_2);
  or or_2 (or_2_out, p[3], p[2], p[1], g[0]);
  or or_3 (or_3_out, p[3], p[2], g[1]);
  or or_4 (or_4_out, p[3], g[2]);
  and and_2 (G_2, g[3], or_4_out, or_3_out, or_2_out);
  or or_5 (P_2, p[3], p[2], p[1], p[0]);
  or or_6 (or_6_out, p[2], p[1], p[0], c_0);
  or or_7 (or_7_out, p[2], p[1], g[0]);
  or or_8 (or_8_out, p[2], g[1]);
  and and_3 (c3, g[2], or_8_out, or_7_out, or_6_out);
  or or_9 (or_9_out, p[1], p[0], c_0);
  or or_10 (or_10_out, p[1], g[0]);
  xnor xnor_1 (S[3], c3, p[3]);
  and and_4 (c2, g[1], or_10_out, or_9_out);
  xnor xnor_2 (S[2], c2, p[2]);
  xnor xnor_3 (S[1], c1, p[1]);
  or or_11 (or_11_out, p[0], c_0);
  and and_5 (c1, g[0], or_11_out);
  xnor xnor_4 (S[0], c_0, p[0]);

  // Other names for the same wires on the sheet: c_1 = c1; c_2 = c2; c_3 = c3; g_0 = g[0]; g_1 = g[1]; g_2_t = g[2];
  //   g_3 = g[3]; p_0 = p[0]; p_1 = p[1]; p_2_t = p[2]; p_3 = p[3]
endmodule
