// Digital circuit 4BitCLA_Extended_D.dig as structural Verilog
module _4BitCLA_Extended_D (
  input  c_0,
  input  [3:0] p,
  input  [3:0] g,
  output [3:0] S,
  output P_2,
  output G_2,
  output c1,
  output c2,
  output c3,
  output c_out
);

  wire andd_1_p3, ord_2_p3, ord_3_p2, ord_4_p1, ord_6_p3, ord_7_p2, ord_8_p1, ord_9_p3, ord_10_p1, ord_11_p2;

  // AndD #(.generic("inputCount := 2;")) andd_1: pin names not known; wires that end beside it: c_out, G_2, andd_1_p3
  // OrD #(.generic("inputCount := 2;")) ord_1: pin names not known; wires that end beside it: andd_1_p3, P_2, c_0
  // OrD #(.generic("inputCount := 4;")) ord_2: pin names not known; wires that end beside it: g[0], p[1], ord_2_p3, p[2], p[3], g[1]
  // OrD #(.generic("inputCount := 3;")) ord_3: pin names not known; wires that end beside it: p[2], ord_3_p2, p[3], g[2]
  // OrD #(.generic("inputCount := 2;")) ord_4: pin names not known; wires that end beside it: ord_4_p1, p[3]
  // AndD #(.generic("inputCount := 4;")) andd_2: pin names not known; wires that end beside it: ord_2_p3, ord_3_p2, G_2, ord_4_p1, g[3], p[0]
  // OrD #(.generic("inputCount := 4;")) ord_5: pin names not known; wires that end beside it: p[1], P_2, p[2], p[3]
  // OrD #(.generic("inputCount := 4;")) ord_6: pin names not known; wires that end beside it: c_0, p[0], ord_6_p3, p[1], p[2], g[0]
  // OrD #(.generic("inputCount := 3;")) ord_7: pin names not known; wires that end beside it: p[1], ord_7_p2, p[2], g[1]
  // OrD #(.generic("inputCount := 2;")) ord_8: pin names not known; wires that end beside it: ord_8_p1, p[2]
  // AndD #(.generic("inputCount := 4;")) andd_3: pin names not known; wires that end beside it: ord_6_p3, ord_7_p2, c3, ord_8_p1, g[2]
  // OrD #(.generic("inputCount := 3;")) ord_9: pin names not known; wires that end beside it: c_0, p[0], ord_9_p3, p[1], g[0]
  // OrD #(.generic("inputCount := 2;")) ord_10: pin names not known; wires that end beside it: ord_10_p1, p[1]
  // XnorD #(.generic("inputCount := 2;")) xnord_1: pin names not known; wires that end beside it: p[3], S[3], c3
  // AndD #(.generic("inputCount := 3;")) andd_4: pin names not known; wires that end beside it: ord_9_p3, ord_10_p1, c2, g[1]
  // XnorD #(.generic("inputCount := 2;")) xnord_2: pin names not known; wires that end beside it: p[2], S[2], c2
  // XnorD #(.generic("inputCount := 2;")) xnord_3: pin names not known; wires that end beside it: p[1], S[1], c1
  // OrD #(.generic("inputCount := 2;")) ord_11: pin names not known; wires that end beside it: c_0, ord_11_p2, p[0]
  // AndD #(.generic("inputCount := 2;")) andd_5: pin names not known; wires that end beside it: ord_11_p2, c1, g[0]
  // XnorD #(.generic("inputCount := 2;")) xnord_4: pin names not known; wires that end beside it: p[0], S[0], c_0

  // Other names for the same wires on the sheet: c_1 = c1; c_2 = c2; c_3 = c3; g_0 = g[0]; g_1 = g[1]; g_2_t = g[2];
  //   g_3 = g[3]; p_0 = p[0]; p_1 = p[1]; p_2_t = p[2]; p_3 = p[3]
endmodule
