// Digital circuit 4BitPG_Generator.dig as structural Verilog
module _4BitPG_Generator (
  input  [3:0] x,
  input  [3:0] y,
  output [3:0] p,
  output [3:0] g
);

  generator generator_1 (.x_i(x[3]), .y_i(y[3]), .g_i(g[3]), .p_i(p[3]));  // open: c_i
  generator generator_2 (.x_i(x[2]), .y_i(y[2]), .g_i(g[2]), .p_i(p[2]));  // open: c_i
  generator generator_3 (.x_i(x[1]), .y_i(y[1]), .g_i(g[1]), .p_i(p[1]));  // open: c_i
  generator generator_4 (.x_i(x[0]), .y_i(y[0]), .g_i(g[0]), .p_i(p[0]));  // open: c_i
endmodule
