// Digital circuit HazardFree.dig as structural Verilog
module HazardFree (
  input  A,
  input  B,
  input  C,
  input  D,
  output C1,
  output C2
);

  wire A_t, and_1_out, and_2_out, and_3_out, and_4_out, B_t, C_t, D_t, or_1_out, or_2_out, or_3_out,
       or_4_out, or_5_out;

  not not_1 (A_t, A);
  not not_2 (B_t, B);
  not not_3 (C_t, C);
  not not_4 (D_t, D);
  and and_1 (and_1_out, A_t, D_t);
  and and_2 (and_2_out, C, D);
  and and_3 (and_3_out, D_t, C_t);
  and and_4 (and_4_out, A, D);
  or or_1 (or_1_out, D_t, B, A);
  or or_2 (or_2_out, C_t, B_t, A);
  or or_3 (or_3_out, D, B_t, A_t);
  or or_4 (or_4_out, C, B, A_t);
  or or_5 (or_5_out, D, C, A_t);
  or or_6 (C1, and_1_out, and_2_out, and_3_out, and_4_out);
  and and_5 (C2, or_1_out, or_2_out, or_3_out, or_4_out, or_5_out);
endmodule

/* Test case:
X		Y		Cin		S		Cout
0		0		0		0		0
1		2		0		3		0
32767		32768		0		65535		0
65535		0		0		65535		0
65535		0		1		0		1
32768		32768		0		0		1
65535		1		0		0		1
65535		65535		0		65534		1
65535		65535		1		65535		1
0		65535		1		0		1
12345		54321		0		1130		1
40000		30000		0		70000		1
40000		30000		1		70001		1
0		1		0		1		0
1		0		1		2		0
65535		1		1		1		1
1024		2048		0		3072		0
1024		2048		1		3073		0
50000		30000		0		14464		1
50000		30000		1		14465		1
0		32767		1		32768		0
32768		0		1		32769		0
1		1		1		3		0
12345		53190		0		65535		0
12345		53191		0		0		1
12345		53191		1		1		1
*/
