// Digital circuit HazardFree_D.dig as structural Verilog
module HazardFree_D (
  input  A,
  input  B,
  input  C,
  input  D,
  output C1,
  output C2
);

  wire A_t, andd_1_p3, andd_2_p3, andd_3_p3, andd_4_p3, B_t, C_t, D_t, ord_1_p4, ord_2_p4, ord_3_p4,
       ord_4_p4, ord_5_p4;

  // NotD #(.generic("inputCount := 1;")) notd_1: pin names not known; wires that end beside it: A, A_t
  // NotD #(.generic("inputCount := 1;")) notd_2: pin names not known; wires that end beside it: B, B_t
  // NotD #(.generic("inputCount := 1;")) notd_3: pin names not known; wires that end beside it: C, C_t
  // NotD #(.generic("inputCount := 1;")) notd_4: pin names not known; wires that end beside it: D, D_t
  // AndD #(.generic("inputCount := 2;")) andd_1: pin names not known; wires that end beside it: A_t, D_t, andd_1_p3
  // AndD #(.generic("inputCount := 2;")) andd_2: pin names not known; wires that end beside it: C, D, andd_2_p3
  // AndD #(.generic("inputCount := 2;")) andd_3: pin names not known; wires that end beside it: D_t, C_t, andd_3_p3
  // AndD #(.generic("inputCount := 2;")) andd_4: pin names not known; wires that end beside it: A, D, andd_4_p3
  // OrD #(.generic("inputCount := 3;")) ord_1: pin names not known; wires that end beside it: D_t, B, A, ord_1_p4
  // OrD #(.generic("inputCount := 3;")) ord_2: pin names not known; wires that end beside it: C_t, B_t, A, ord_2_p4
  // OrD #(.generic("inputCount := 3;")) ord_3: pin names not known; wires that end beside it: D, B_t, A_t, ord_3_p4
  // OrD #(.generic("inputCount := 3;")) ord_4: pin names not known; wires that end beside it: C, B, A_t, ord_4_p4
  // OrD #(.generic("inputCount := 3;")) ord_5: pin names not known; wires that end beside it: D, C, A_t, ord_5_p4
  // OrD #(.generic("inputCount := 4;")) ord_6: pin names not known; wires that end beside it: andd_1_p3, andd_2_p3, andd_3_p3, andd_4_p3, C1
  // AndD #(.generic("inputCount := 5;")) andd_5: pin names not known; wires that end beside it: ord_1_p4, ord_2_p4, ord_3_p4, ord_4_p4, ord_5_p4, C2
endmodule

/* Test case:
X		Y		Cin		S		Cout
0		0		0		0		0
1		2		0		3		0
32767		32768		0		65535		0
65535		0		0		65535		0
65535		0		1		0		1
32768		32768		0		0		1
65535		1		0		0		1
65535		65535		0		65534		1
65535		65535		1		65535		1
0		65535		1		0		1
12345		54321		0		1130		1
40000		30000		0		70000		1
40000		30000		1		70001		1
0		1		0		1		0
1		0		1		2		0
65535		1		1		1		1
1024		2048		0		3072		0
1024		2048		1		3073		0
50000		30000		0		14464		1
50000		30000		1		14465		1
0		32767		1		32768		0
32768		0		1		32769		0
1		1		1		3		0
12345		53190		0		65535		0
12345		53191		0		0		1
12345		53191		1		1		1
*/
