// Digital circuit TwoLevelCLA.dig as structural Verilog
module TwoLevelCLA (
  input  Cin,
  input  [15:0] X,
  input  [15:0] Y,
  output Cout,
  output [15:0] S
);

  wire _4bitcla_1_p5, _4bitcla_2_p5, _4bitcla_3_p5;
  wire [3:0] _4bitpg_generator_1_g, _4bitpg_generator_1_p, _4bitpg_generator_2_g, _4bitpg_generator_2_p,
       _4bitpg_generator_3_g, _4bitpg_generator_3_p, _4bitpg_generator_4_g, _4bitpg_generator_4_p, G, P;

  _4BitPG_Generator _4bitpg_generator_1 (
    .x(X[15:12]), .y(Y[15:12]), .p(_4bitpg_generator_1_p), .g(_4bitpg_generator_1_g));
  // _4BitCLA _4bitcla_1: pin names not known; wires that end beside it: _4bitpg_generator_1_g, G[3], _4bitpg_generator_1_p, P[3], _4bitcla_1_p5, S[15:12]
  _4BitPG_Generator _4bitpg_generator_2 (
    .x(X[11:8]), .y(Y[11:8]), .p(_4bitpg_generator_2_p), .g(_4bitpg_generator_2_g));
  // _4BitCLA _4bitcla_2: pin names not known; wires that end beside it: _4bitpg_generator_2_g, G[2], _4bitpg_generator_2_p, P[2], _4bitcla_2_p5, S[11:8]
  _4BitPG_Generator _4bitpg_generator_3 (.x(X[7:4]), .y(Y[7:4]), .p(_4bitpg_generator_3_p), .g(_4bitpg_generator_3_g));
  // _4BitCLA _4bitcla_3: pin names not known; wires that end beside it: _4bitpg_generator_3_g, G[1], _4bitpg_generator_3_p, P[1], _4bitcla_3_p5, S[7:4]
  _4BitPG_Generator _4bitpg_generator_4 (.x(X[3:0]), .y(Y[3:0]), .p(_4bitpg_generator_4_p), .g(_4bitpg_generator_4_g));
  // _4BitCLA _4bitcla_4: pin names not known; wires that end beside it: _4bitpg_generator_4_g, G[0], _4bitpg_generator_4_p, P[0], Cin, S[3:0]
  _4BitCLA_Extended _4bitcla_extended_1 (
    .c_0(Cin), .p(P), .g(G), .c1(_4bitcla_3_p5), .c2(_4bitcla_2_p5), .c3(_4bitcla_1_p5), .c_out(Cout));  // open: S, P_2, G_2
endmodule

/* Test case:
X		Y		Cin		S		Cout
0		0		0		0		0
1		2		0		3		0
32767		32768		0		65535		0
65535		0		0		65535		0
65535		0		1		0		1
32768		32768		0		0		1
65535		1		0		0		1
65535		65535		0		65534		1
65535		65535		1		65535		1
0		65535		1		0		1
12345		54321		0		1130		1
40000		30000		0		70000		1
40000		30000		1		70001		1
0		1		0		1		0
1		0		1		2		0
65535		1		1		1		1
1024		2048		0		3072		0
1024		2048		1		3073		0
50000		30000		0		14464		1
50000		30000		1		14465		1
0		32767		1		32768		0
32768		0		1		32769		0
1		1		1		3		0
12345		53190		0		65535		0
12345		53191		0		0		1
12345		53191		1		1		1
*/
