// Digital circuit generator.dig as structural Verilog
module generator (
  input  x_i,
  input  y_i,
  input  c_i,
  output g_i,
  output p_i
);

  or or_1 (g_i, x_i, y_i);
  xnor xnor_1 (p_i, x_i, y_i);

  // Other names for the same wires on the sheet: c = c_i; g = g_i; p = p_i; x = x_i; y = y_i
endmodule
