// Digital circuit generatorD.dig as structural Verilog
module generatorD (
  input  x_i,
  input  y_i,
  output g_i,
  output p_i
);

  // OrD #(.generic("inputCount := 2;")) ord_1: pin names not known; wires that end beside it: x_i, y_i, g_i
  // XnorD #(.generic("inputCount := 2;")) xnord_1: pin names not known; wires that end beside it: x_i, y_i, p_i

  // Other names for the same wires on the sheet: g = g_i; p = p_i; x = x_i; y = y_i

  // Notes on the sheet:
  //   x_i+y_i
  //   x_i⊙y_i
endmodule
