// Digital circuit BoothsMultiplierMealy.dig as structural Verilog
module BoothsMultiplierMealy (
  input  CLR,
  input  [12:0] MULTIPLIER,
  input  [12:0] MULTIPLICAND,
  input  CLK,
  output DONE,
  output [1:0] OP_DONE,
  output [25:0] RESULT
);

  wire ACCUMULATOR_p3, and_1_out, and_2_out, F2_q, mealycontroller_1_p6, mealycontroller_1_p7, MULTIPLIER_p3,
       MULTIPLIER_p4, xor_1_out;
  wire [3:0] counter_1_out;
  wire [12:0] ACCUMULATOR_p6, add_1_s, sub_1_s;

  xor xor_1 (xor_1_out, MULTIPLICAND[12], mealycontroller_1_p7);
  D_FF_AS F2 (.Set(1'b0), .D(xor_1_out), .C(ACCUMULATOR_p3), .Clr(CLR), .Q(F2_q));  // open: nQ
  Counter #(.Bits(4)) counter_1 (.en(and_1_out), .C(CLK), .clr(CLR), .out(counter_1_out));  // open: ovf
  and and_1 (and_1_out, MULTIPLIER_p4, ~and_2_out);  // And
  and and_2 (and_2_out, counter_1_out[0], ~counter_1_out[1], counter_1_out[2], counter_1_out[3]);  // And
  // Shifter MULTIPLIER: pin names not known; wires that end beside it: CLK, CLR, MULTIPLIER_p3, MULTIPLIER_p4, RESULT[13], MULTIPLIER, {RESULT[12:1], OP_DONE[0]}
  // Shifter ACCUMULATOR: pin names not known; wires that end beside it: CLK, CLR, ACCUMULATOR_p3, MULTIPLIER_p4, F2_q, ACCUMULATOR_p6, RESULT[25:13]
  Register F1 (.D(OP_DONE[0]), .C(CLK), .en(1'b1), .Q(OP_DONE[1]));
  // MealyController mealycontroller_1: pin names not known; wires that end beside it: OP_DONE[0], CLK, CLR, and_2_out, MULTIPLIER_p3, mealycontroller_1_p6, mealycontroller_1_p7, MULTIPLIER_p4, DONE
  Add #(.Bits(13)) add_1 (.a(RESULT[25:13]), .b(MULTIPLICAND), .c_i(1'b0), .s(add_1_s));  // open: c_o
  Sub #(.Bits(13)) sub_1 (.a(RESULT[25:13]), .b(MULTIPLICAND), .c_i(1'b0), .s(sub_1_s));  // open: c_o
  Multiplexer #(.Bits(13)) multiplexer_1 (
    .sel(mealycontroller_1_p7), .in_0(add_1_s), .in_1(sub_1_s), .out(ACCUMULATOR_p6));
  or or_1 (ACCUMULATOR_p3, mealycontroller_1_p6, mealycontroller_1_p7);

  assign RESULT[0] = OP_DONE[0];

  // Other names for the same wires on the sheet: CLK_T = CLK

  // Notes on the sheet:
  //   MULTIPLIER: default 2
  //   MULTIPLICAND: default -8
  //   CLK: Hz: 20
endmodule
