// Digital circuit BoothsMultiplierMoore.dig as structural Verilog
module BoothsMultiplierMoore (
  input  CLR,
  input  [12:0] MULTIPLIER,
  input  [12:0] MULTIPLICAND,
  input  CLK,
  output DONE,
  output [1:0] OP_DONE,
  output [25:0] RESULT
);

  wire and_1_out, and_2_out, and_3_out, and_4_out, F2_q, moorecontroller_1_add, moorecontroller_1_shift,
       moorecontroller_1_subtract, MULTIPLIER_p3, or_1_out, xor_1_out;
  wire [3:0] counter_1_out;
  wire [12:0] ACCUMULATOR_p6, add_1_s, sub_1_s;

  xor xor_1 (xor_1_out, MULTIPLICAND[12], moorecontroller_1_subtract);
  D_FF_AS F2 (.Set(1'b0), .D(xor_1_out), .C(or_1_out), .Clr(CLR), .Q(F2_q));  // open: nQ
  Counter #(.Bits(4)) counter_1 (.en(and_1_out), .C(CLK), .clr(CLR), .out(counter_1_out));  // open: ovf
  and and_1 (and_1_out, moorecontroller_1_shift, ~and_2_out);  // And
  and and_2 (and_2_out, counter_1_out[0], ~counter_1_out[1], counter_1_out[2], counter_1_out[3]);  // And
  and and_3 (and_3_out, moorecontroller_1_shift, ~and_2_out);  // And
  and and_4 (and_4_out, or_1_out, ~and_2_out);  // And
  // Shifter MULTIPLIER: pin names not known; wires that end beside it: CLK, CLR, MULTIPLIER_p3, and_3_out, RESULT[13], MULTIPLIER, {RESULT[12:1], OP_DONE[0]}
  // Shifter ACCUMULATOR: pin names not known; wires that end beside it: CLK, CLR, and_4_out, and_3_out, F2_q, ACCUMULATOR_p6, RESULT[25:13]
  Register F1 (.D(OP_DONE[0]), .C(CLK), .en(1'b1), .Q(OP_DONE[1]));
  MooreController moorecontroller_1 (
    .CURRENT_SHIFT(MULTIPLIER[0]), .SHIFT_IN(RESULT[1]), .CLK(CLK), .RST(CLR), .COMPLETED(and_2_out),
    .INIT(MULTIPLIER_p3), .ADD(moorecontroller_1_add), .SUBTRACT(moorecontroller_1_subtract),
    .SHIFT(moorecontroller_1_shift), .END(DONE));  // open: EX_OP
  Add #(.Bits(13)) add_1 (.a(RESULT[25:13]), .b(MULTIPLICAND), .c_i(1'b0), .s(add_1_s));  // open: c_o
  Sub #(.Bits(13)) sub_1 (.a(RESULT[25:13]), .b(MULTIPLICAND), .c_i(1'b0), .s(sub_1_s));  // open: c_o
  Multiplexer #(.Bits(13)) multiplexer_1 (
    .sel(moorecontroller_1_subtract), .in_0(add_1_s), .in_1(sub_1_s), .out(ACCUMULATOR_p6));
  or or_1 (or_1_out, moorecontroller_1_add, moorecontroller_1_subtract);

  assign RESULT[0] = OP_DONE[0];

  // Other names for the same wires on the sheet: CLK_T = CLK

  // Notes on the sheet:
  //   MULTIPLIER: default 2
  //   MULTIPLICAND: default -8
  //   CLK: Hz: 20
endmodule
