// Digital circuit DFF.dig as structural Verilog
module DFF (
  input  D,
  input  CLK,
  output Q,
  output QN
);

  wire not_1_out;

  RS_FF rs_ff_1 (.S(D), .C(CLK), .R(not_1_out), .Q(Q), .nQ(QN));
  not not_1 (not_1_out, D);
endmodule
