// Digital circuit MealyController.dig as structural Verilog
module MealyController (
  input  X,
  input  clk,
  input  CLR,
  output A,
  output S,
  output END,
  output SHIFT,
  output INIT
);

  wire and_1_out, and_4_out, and_5_out, and_6_out, and_7_out, and_8_out, and_12_out, N_in, nor_1_out,
       nor_2_out, nor_3_out, nor_5_out, nor_6_out, or_1_out, or_2_out, or_3_out, or_4_out, or_5_out, Q_0in,
       Q_0Nin, Q_1in, Q_1Nin;
  wire [3:0] counter_1_out;

  and and_1 (and_1_out, ~N_in, 1'b1);  // And
  Counter #(.Bits(4)) counter_1 (.en(and_1_out), .C(clk), .clr(CLR), .out(counter_1_out));  // open: ovf
  // Probe on counter_1_out
  and and_2 (INIT, ~counter_1_out[0], ~counter_1_out[1], ~counter_1_out[2], ~counter_1_out[3]);  // And
  nor nor_1 (nor_1_out, Q_0in, Q_1Nin, ~X, N_in);  // NOr
  nor nor_2 (nor_2_out, N_in, X, Q_0Nin, Q_1Nin);
  and and_3 (N_in, counter_1_out[0], counter_1_out[1], ~counter_1_out[2], counter_1_out[3]);  // And
  // Probe on nor_1_out
  // Probe on nor_2_out
  // Probe CLK_int on clk
  // Probe N_int on N_in
  and and_4 (and_4_out, Q_1in, Q_0Nin, ~N_in, ~X);  // And
  and and_5 (and_5_out, Q_0in, Q_1in, ~N_in, X);  // And
  // Probe INIT_int on INIT
  and and_6 (and_6_out, ~INIT, ~N_in);  // And
  or or_1 (or_1_out, INIT, ~clk);  // Or
  or or_2 (or_2_out, N_in, INIT);
  and and_7 (and_7_out, Q_0Nin, Q_1in, X, ~N_in);  // And
  and and_8 (and_8_out, Q_0in, Q_1in, ~N_in, ~X);  // And
  or or_3 (or_3_out, and_4_out, and_5_out);
  // Probe 2 on or_1_out
  // Probe 3 on or_2_out
  // Probe S_int on and_7_out
  and and_9 (S, and_7_out, clk);
  // Probe A_int on and_8_out
  and and_10 (A, and_8_out, clk);
  // Probe SHIFT_int on or_3_out
  // Probe 1 on and_6_out
  RS_FF rs_ff_1 (.S(and_6_out), .C(or_1_out), .R(or_2_out), .Q(Q_1in), .nQ(Q_1Nin));
  and and_11 (SHIFT, or_3_out, clk);
  nor nor_3 (nor_3_out, X, N_in);
  nor nor_4 (END, Q_1Nin, ~N_in);  // NOr
  nor nor_5 (nor_5_out, Q_0in, Q_1in, N_in);
  or or_4 (or_4_out, nor_3_out, INIT);
  // Probe on nor_5_out
  or or_5 (or_5_out, INIT, ~clk);  // Or
  nor nor_6 (nor_6_out, ~X, Q_1Nin);  // NOr
  and and_12 (and_12_out, ~INIT, nor_6_out);  // And
  RS_FF rs_ff_2 (.S(and_12_out), .C(or_5_out), .R(or_4_out), .Q(Q_0in), .nQ(Q_0Nin));
  // Probe Q on {Q_1in, Q_0in}

  // Other names for the same wires on the sheet: CLR_in = CLR; INIT_in = INIT; X_in = X
endmodule
