// Digital circuit MooreController.dig as structural Verilog
module MooreController (
  input  CURRENT_SHIFT,
  input  SHIFT_IN,
  input  CLK,
  input  RST,
  input  COMPLETED,
  output INIT,
  output ADD,
  output SUBTRACT,
  output SHIFT,
  output [1:0] EX_OP,
  output END
);

  wire and_1_out, and_9_out, and_10_out, and_11_out, and_12_out, and_13_out, and_14_out, and_15_out,
       and_16_out, C_in, or_1_out, or_2_out, or_3_out, or_4_out, or_5_out, Q0, Q0_nq, Q1, Q1_nq, Q2, Q2_nq,
       xnor_1_out, xnor_2_out;

  and and_1 (and_1_out, SHIFT_IN, Q2);
  and and_2 (C_in, CURRENT_SHIFT, ~Q2, ~Q1, ~Q0);  // And
  xnor xnor_1 (xnor_1_out, Q1, Q0);
  xnor xnor_2 (xnor_2_out, Q1, Q0);
  // And and_3 has open pins: In_1=COMPLETED, In_2=Q2, In_3=xnor_1_out, out=open
  and and_4 (INIT, ~Q2, ~Q1, ~Q0);  // And
  and and_5 (ADD, Q2, ~Q1, Q0);  // And
  and and_6 (SUBTRACT, Q2, Q1, ~Q0);  // And
  and and_7 (SHIFT, xnor_2_out, Q2);
  and and_8 (END, ~Q2, ~Q1, Q0);  // And
  and and_9 (and_9_out, Q2_nq, ~COMPLETED);  // And
  and and_10 (and_10_out, COMPLETED, Q2);
  and and_11 (and_11_out, Q0_nq, and_1_out);
  and and_12 (and_12_out, Q0, ~and_1_out);  // And
  and and_13 (and_13_out, Q1, ~RST);  // And
  or or_1 (or_1_out, Q1_nq, RST);
  or or_2 (or_2_out, RST, and_10_out);
  or or_3 (or_3_out, C_in, and_11_out);
  or or_4 (or_4_out, RST, and_12_out);
  or or_5 (or_5_out, and_13_out, COMPLETED);
  and and_14 (and_14_out, and_9_out, ~RST);  // And
  and and_15 (and_15_out, ~RST, or_3_out);  // And
  and and_16 (and_16_out, ~COMPLETED, or_1_out);  // And
  PriorityEncoder #(.Selector_Bits(2)) priorityencoder_1 (
    .in0(INIT), .in1(ADD), .in2(SUBTRACT), .in3(SHIFT), .num(EX_OP));  // open: any
  RS_FF u_Q2 (.S(and_14_out), .C(CLK), .R(or_2_out), .Q(Q2), .nQ(Q2_nq));
  RS_FF u_Q1 (.S(and_15_out), .C(CLK), .R(or_4_out), .Q(Q1), .nQ(Q1_nq));
  RS_FF u_Q0 (.S(or_5_out), .C(CLK), .R(and_16_out), .Q(Q0), .nQ(Q0_nq));

  // Other names for the same wires on the sheet: CLK_in = CLK; CLR_in = RST; Complete_in = COMPLETED
endmodule
