// Digital circuit PTFF.dig as structural Verilog
module PTFF (
  input  P,
  input  CLK,
  input  T,
  output Q,
  output QN
);

  wire xor_1_out;

  JK_FF jk_ff_1 (.J(P), .C(CLK), .K(xor_1_out), .Q(Q), .nQ(QN));
  xor xor_1 (xor_1_out, P, T);
endmodule
