// Digital circuit RefundSerializer.dig as structural Verilog
module RefundSerializer (
  input  [1:0] REFUND_AMT,
  input  LOAD,
  input  COUNT_3,
  input  CLK,
  output [1:0] BILL_OUT,
  output BUSY
);

  wire and_1_out, and_3_out, and_4_out, multiplexer_1_out, multiplexer_2_out, Q0_in, Q0N_in, Q1_in, Q1N_in,
       xor_1_out;

  and and_1 (and_1_out, ~COUNT_3, Q1_in);  // And
  xor xor_1 (xor_1_out, Q1_in, Q0_in);
  or or_1 (BUSY, Q1_in, Q0_in);
  or or_2 (BILL_OUT[0], xor_1_out, and_1_out);
  and and_2 (BILL_OUT[1], Q1_in, Q0_in, COUNT_3);
  and and_3 (and_3_out, Q1_in, Q0_in, ~COUNT_3);  // And
  and and_4 (and_4_out, Q1_in, Q0N_in);
  Multiplexer multiplexer_1 (.sel(LOAD), .in_0(and_3_out), .in_1(REFUND_AMT[1]), .out(multiplexer_1_out));
  Multiplexer multiplexer_2 (.sel(LOAD), .in_0(and_4_out), .in_1(REFUND_AMT[0]), .out(multiplexer_2_out));
  D_FF_AS Q1 (.Set(1'b0), .D(multiplexer_1_out), .C(CLK), .Clr(1'b0), .Q(Q1_in), .nQ(Q1N_in));
  D_FF_AS Q0 (.Set(1'b0), .D(multiplexer_2_out), .C(CLK), .Clr(1'b0), .Q(Q0_in), .nQ(Q0N_in));

  // Other names for the same wires on the sheet: CLK_in = CLK; X_in = COUNT_3
endmodule
