// Digital circuit SRFF.dig as structural Verilog
module SRFF (
  input  P,
  input  CLK,
  input  T,
  output Q,
  output QN
);

  wire and_1_out;

  and and_1 (and_1_out, P, QN);
  PTFF ptff_1 (.P(and_1_out), .CLK(CLK), .T(T), .Q(Q), .QN(QN));
endmodule
