// Digital circuit VendingMachine.dig as structural Verilog
module VendingMachine (
  input  [1:0] X,
  input  CLK,
  input  RST,
  output [1:0] Z,
  output [1:0] C
);

  wire and_1_out, and_2_out, and_3_out, and_5_out, and_6_out, and_7_out, and_8_out, or_1_out, or_3_out,
       Q0_in, Q0N_in, Q1_in, Q1N_in;

  and and_1 (and_1_out, Q1N_in, Q0_in, X[0]);
  and and_2 (and_2_out, Q0N_in, Q1_in, X[0]);
  and and_3 (and_3_out, ~X[0], X[1], Q0N_in, Q1N_in);  // And
  and and_4 (Z[1], Q1_in, Q0_in, X[1], X[0]);
  and and_5 (and_5_out, X[1], Q1_in);
  and and_6 (and_6_out, X[0], Q0_in);
  and and_7 (and_7_out, X[1], X[0]);
  or or_1 (or_1_out, X[1], X[0]);
  or or_2 (Z[0], and_5_out, and_6_out, and_7_out);
  or or_3 (or_3_out, and_1_out, and_2_out, and_3_out);
  and and_8 (and_8_out, or_1_out, Q0N_in);
  D_FF_AS Q_1 (.Set(1'b0), .D(or_3_out), .C(CLK), .Clr(RST), .Q(Q1_in), .nQ(Q1N_in));
  D_FF_AS Q_0 (.Set(1'b0), .D(and_8_out), .C(CLK), .Clr(RST), .Q(Q0_in), .nQ(Q0N_in));
  and and_9 (C[0], ~X[1], ~X[0], Q0_in);  // And
  and and_10 (C[1], ~X[1], ~X[0], Q1_in);  // And
  // Probe Q on {Q1_in, Q0_in}

  // Other names for the same wires on the sheet: C0_out = C[0]; C1_out = C[1]; CLK_in = CLK; CLR_in = RST;
  //   X0_in = X[0]; X1_in = X[1]; Z0_out = Z[0]; Z1_out = Z[1]
endmodule
