// Digital circuit VendingMachine3.dig as structural Verilog
module VendingMachine3 (
  input  [1:0] BILL,
  input  CLK,
  input  RST,
  output [1:0] CHOCOLATE,
  output [1:0] REFUND_AMT,
  output EMPTY,
  output BUSY
);

  wire and_1_out, and_2_out, and_4_out, and_5_out, and_6_out, and_7_out, and_8_out, chocolatecounter_1_p5,
       CLK_in, or_1_out, or_2_out, or_4_out, Q0_in, Q0N_in, Q1_in, Q1N_in, xnor_1_out, xor_1_out;

  xor xor_1 (xor_1_out, Q1_in, Q0_in);
  xnor xnor_1 (xnor_1_out, Q1_in, Q0_in);
  and and_1 (and_1_out, xor_1_out, BILL[0]);
  and and_2 (and_2_out, BILL[1], ~BILL[0], xnor_1_out);  // And
  and and_3 (CHOCOLATE[1], Q1_in, Q0_in, BILL[1], BILL[0]);
  and and_4 (and_4_out, BILL[1], Q1_in);
  and and_5 (and_5_out, BILL[1], Q0_in);
  and and_6 (and_6_out, BILL[1], Q1N_in, BILL[0]);
  and and_7 (and_7_out, Q1_in, Q0_in, BILL[0]);
  or or_1 (or_1_out, BILL[1], BILL[0]);
  // Probe Q on {Q1_in, Q0_in}
  or or_2 (or_2_out, and_1_out, and_2_out);
  and and_8 (and_8_out, or_1_out, Q0N_in);
  or or_3 (CHOCOLATE[0], and_4_out, and_5_out, and_6_out, and_7_out);
  D_FF_AS Q_1 (.Set(1'b0), .D(or_2_out), .C(CLK_in), .Clr(RST), .Q(Q1_in), .nQ(Q1N_in));
  D_FF_AS Q_0 (.Set(1'b0), .D(and_8_out), .C(CLK_in), .Clr(RST), .Q(Q0_in), .nQ(Q0N_in));
  and and_9 (REFUND_AMT[0], ~BILL[1], ~BILL[0], Q0_in);  // And
  and and_10 (REFUND_AMT[1], ~BILL[1], ~BILL[0], Q1_in);  // And
  or or_4 (or_4_out, Q1_in, Q0_in);
  nand nand_1 (BUSY, or_4_out, ~BILL[1], ~BILL[0]);  // NAnd
  // ChocolateCounter chocolatecounter_1: pin names not known; wires that end beside it: CHOCOLATE, CLK_in, RST, EMPTY, chocolatecounter_1_p5
  // Probe on chocolatecounter_1_p5
  and and_11 (CLK_in, CLK, ~EMPTY);  // And

  // Other names for the same wires on the sheet: X0_in = BILL[0]; X1_in = BILL[1]; C0_out = REFUND_AMT[0];
  //   C1_out = REFUND_AMT[1]; CLR_in = RST; Z0_out = CHOCOLATE[0]; Z1_out = CHOCOLATE[1]
endmodule
