// Digital circuit VendingMachineTop3.dig as structural Verilog
module VendingMachineTop3 (
  input  [1:0] BILL,
  input  CLK,
  input  RST
);

  wire CLK_in, decoder_1_out_1, decoder_1_out_2, decoder_1_out_3, decoder_2_out_1, decoder_2_out_2,
       not_1_out, or_1_out, or_2_out, or_3_out, refundserializer_1_busy, vendingmachine3_1_busy,
       vendingmachine3_1_empty;
  wire [1:0] refundserializer_1_bill_out, vendingmachine3_1_chocolate, vendingmachine3_1_refund_amt;
  wire [7:0] _1_Counter_out, _3_Counter_out, _5_Counter_out;

  Decoder #(.Selector_Bits(2)) decoder_1 (
    .sel(BILL), .out_1(decoder_1_out_1), .out_2(decoder_1_out_2), .out_3(decoder_1_out_3));  // open: out_0
  VendingMachine3 vendingmachine3_1 (
    .BILL(BILL), .CLK(CLK_in), .RST(RST), .CHOCOLATE(vendingmachine3_1_chocolate),
    .REFUND_AMT(vendingmachine3_1_refund_amt), .EMPTY(vendingmachine3_1_empty), .BUSY(vendingmachine3_1_busy));
  or or_1 (or_1_out, decoder_2_out_2, decoder_1_out_2);
  CounterPreset #(.maxValue(255), .Bits(8)) _3_Counter (
    .en(or_1_out), .C(CLK_in), .dir(refundserializer_1_busy), .in(8'h1f), .ld(RST), .clr(1'b0),
    .out(_3_Counter_out));  // open: ovf
  or or_2 (or_2_out, decoder_2_out_1, decoder_1_out_1);
  CounterPreset #(.maxValue(255), .Bits(8)) _1_Counter (
    .en(or_2_out), .C(CLK_in), .dir(refundserializer_1_busy), .in(8'h1f), .ld(RST), .clr(1'b0),
    .out(_1_Counter_out));  // open: ovf
  // Probe on vendingmachine3_1_chocolate
  // Probe on _3_Counter_out
  // Probe Refund on vendingmachine3_1_refund_amt
  and and_1 (CLK_in, ~vendingmachine3_1_empty, CLK);  // And
  // Probe on _1_Counter_out
  CounterPreset #(.maxValue(255), .Bits(8)) _5_Counter (
    .en(decoder_1_out_3), .C(CLK_in), .dir(refundserializer_1_busy), .in(8'h1f), .ld(RST), .clr(1'b0),
    .out(_5_Counter_out));  // open: ovf
  or or_3 (or_3_out, _3_Counter_out[0], _3_Counter_out[1], _3_Counter_out[2], _3_Counter_out[3], _3_Counter_out[4], _3_Counter_out[5], _3_Counter_out[6], _3_Counter_out[7]);
  not not_1 (not_1_out, vendingmachine3_1_busy);
  // Probe on _5_Counter_out
  RefundSerializer refundserializer_1 (
    .REFUND_AMT(vendingmachine3_1_refund_amt), .LOAD(not_1_out), .COUNT_3(or_3_out), .CLK(CLK_in),
    .BILL_OUT(refundserializer_1_bill_out), .BUSY(refundserializer_1_busy));
  // Probe Bill out on refundserializer_1_bill_out
  Decoder #(.Selector_Bits(2)) decoder_2 (
    .sel(refundserializer_1_bill_out), .out_1(decoder_2_out_1), .out_2(decoder_2_out_2));  // open: out_0, out_3

  // Other names for the same wires on the sheet: CLR_in = RST
endmodule
